# Fritzing sketch cam-solenoid (saved by Fritzing 0.8.7b)
breadboards: 1

parts:
  Part1 = Arduino Uno (Rev3)
  S1 = Pushbutton [package="[THT]"]
  J1 = screw terminal, 2 pins
  L1 = Solenoid
  U2 = Transformer [package=transformer]
  U3 = RELAY-SOLIDSTATE [package=relay-s108t02]
  R1 = Resistor [tolerance=±5% resistance=10k package=THT]

nets:
  N1: Part1.D12/MISO, S1.Pin_3, S1.Pin_4, R1.Pin_1
  N2: Part1.D13/SCK, U3.+
  N3: Part1.GND, S1.Pin_1, S1.Pin_2, U3.-
  N4: Part1.5V, R1.Pin_0
  N5: J1.pin1, U2.2, U3.T1
  N6: J1.pin2, L1.pin1, U3.T2
  N7: L1.pin2, U2.1
